# Fritzing sketch schematic (saved by Fritzing 0.9.9b)
breadboards: 1

parts:
  Part1 = Arduino Uno (Rev3) - ICSP
  J1 = Basic Servo
  MH-ET_LIVE_ESP32_DEVKIT1 = MH-ET LIVE ESP32 DEVKIT 38 pins
  Part2 = RFID-RC522-v2
  Part3 = 4x4 Keypad [part_number=101207]
  Display1 = LCD screen 16x2 IIC [part_number=101290]

nets:
  N1: Part1.A0, Part3.1
  N2: Part1.A1, Part3.2
  N3: Part1.A2, Part3.3
  N4: Part1.A3, Part3.4
  N5: Part1.A4/SDA, Display1.SDA
  N6: Part1.A5/SCL, Display1.SCL
  N7: Part1.D8, J1.pulse
  N8: Part1.D9_PWM, Part2.RST
  N9: Part1.D10_PWM/SS, Part2.SDA
  N10: Part1.D11_PWM/MOSI, Part2.MOSI
  N11: Part1.D12/MISO, Part2.MISO
  N12: Part1.D13/SCK, Part2.SCK
  GND: Part1.GND, J1.gnd, Part2.GND, Display1.GND
  N13: Part1.D2, MH-ET_LIVE_ESP32_DEVKIT1.IO17
  N14: Part1.D3_PWM, MH-ET_LIVE_ESP32_DEVKIT1.IO16
  N15: Part1.D4, Part3.5
  N16: Part1.D5_PWM, Part3.6
  N17: Part1.D6_PWM, Part3.7
  N18: Part1.D7, Part3.8
  3V3: Part1.3V3, Part2.3.3V
  VCC: Part1.5V, J1.vcc, Display1.VCC

custom parts:
  MH-ET LIVE ESP32 DEVKIT 38 pins: http://mh.nodebb.com/topic/2/mh-et-live-esp32-devkit
  RFID-RC522-v2: A simple China made RFID-RC522 Reader; do check the pin labels, as this is a MFRC522 based clone.
  4x4 Keypad: Matrix membrane keypad 4x4
  LCD screen 16x2 IIC: LCD screen with HD44780 controller enables showing text, symbols, value or anything else that comes from Croduino/Arduino. It is capable of showing 16 symbols in two lines and therefore can be used in many projects that need to send clearly visible and legible output information.. • Color of symbols: White • Backlight: Blue • Dimensions: 80 x 36 x 12 mm • Screen dimensions: 64.5 x 16 mm •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
